# Fritzing sketch greenHouse (saved by Fritzing 0.9.3b)

parts:
  Часть1 = Soil Moisture Sensor
  Часть2 = Arduino Nano (Rev3.0)
  LED1 = LEDs [package=led10mm]
  Part3 = Lilypad Battery Connect
  KY-1 = Keyes Relay [package=THT]
  Part4 = Lilypad Battery Connect
  Часть3 = Lilypad Battery Connect
  R1 = RPACK* [package=rpack-sip-pth-5]
  R2 = RPACK* [package=rpack-sip-pth-5]
  ENC28J1 = ENC28J60
  Grove1 = Grove Light Sensor
  DS1 = DS18B20 1-Wire Temperature Sensor [part_number=DS18B20]
  Часть4 = Lilypad Battery Connect
  R3 = RPACK* [package=rpack-sip-pth-5]
  R4 = RPACK* [package=rpack-sip-pth-5]

nets:
  N1: Часть1.GND, R2.3
  N2: Часть1.VCC, R1.3
  N3: Часть2.D4, DS1.DQ
  N4: Часть2.D8, KY-1.signal
  N5: Часть2.D9, ENC28J1.RST
  N6: Часть2.D10, ENC28J1.CS
  N7: Часть2.D11/MOSI, ENC28J1.SO
  N8: Часть2.D12/MISO, ENC28J1.SI
  N9: Часть2.VIN, Part4.+
  N10: Часть2.GND, Part4.-
  N11: Часть2.D13/SCK, ENC28J1.CLK
  N12: LED1.A, Part3.+
  N13: LED1.C, KY-1.NO
  N14: Part3.-, KY-1.C
  N15: KY-1.power, R1.2
  N16: KY-1.ground, R2.2
  N17: Часть3.-, R2.1
  N18: Часть3.+, R1.1
  N19: R1.4, Grove1.VCC
  N20: R1.5, DS1.GND
  N21: R2.5, DS1.VDD
  N22: ENC28J1.3.3, R4.2
  N23: ENC28J1.GND, R3.2
  N24: Часть4.-, R3.1
  N25: Часть4.+, R4.1

notes:
  240V AC power supply
  12V DC power supply
  5V
  Power Supply
  3.3 V power supply

custom parts:
  LEDs: LEDs Standard schematic elements and footprints for 5mm, 3mm, 1206, and 0603 sized LEDs. 5mm - Spark Fun Electronics SKU : COM-00529 (and others)
  Keyes Relay: The Keyes 5V relay module is suitable for SCM development, home appliance control. It uses a 5V~12V TIL control signal which can control DC / AC signal.
  ENC28J60: Ethernet Module ENC28J60
